// Logisim project 755232-4.circ as structural Verilog: 5 circuits, main circuit main
module main (
);

  wire a_t, alu_1_z, b, clk, comparator_1_eq, FZ, fz_t, ir, multiplexer_1_out, nL_E, not_1_out, pc_t, reset,
       tty_out_1_clr, tty_out_1_out, xnor_1_out;
  wire [1:0] alu, mux;
  wire [2:0] rom_1_data;
  wire [3:0] CO;
  wire [4:0] adder_1_out, F, multiplexer_3_out, rom_1_data_3, \µPC_q ;
  wire [6:0] A, adder_2_out, D, D6_0, PC;
  wire [9:0] CICN, INSN;
  wire [13:13] rom_1_data_2;
  wire [15:0] A_q, B_q, ram_1_data;
  wire [15:7] alu_1_out;

  Register #(.width(16)) u_IR (.D(ram_1_data), .en(ir), .Q({CO, F, D}), .clk(clk));  // open: clr
  Multiplexer #(.select(3), .enable("false")) multiplexer_1 (
    .in0(CO[0]), .in1(CO[1]), .in2(CO[2]), .in3(CO[3]), .in4(FZ), .in5(1'b0), .in6(1'b0), .in7(1'b0),
    .out(multiplexer_1_out), .sel(rom_1_data));
  Register #(.width(7)) u_PC (.D(adder_2_out), .en(pc_t), .Q(PC), .clk(clk), .clr(reset));
  xnor xnor_1 (xnor_1_out, multiplexer_1_out, rom_1_data_2[13]);
  Multiplexer #(.select(2), .width(7), .enable("false")) multiplexer_2 (
    .in0(PC), .in2({CO[1:0], F}), .in3(D), .out(A), .sel(mux));  // open: in1
  Multiplexer #(.width(5), .enable("false")) multiplexer_3 (
    .in0(adder_1_out), .in1(rom_1_data_3), .out(multiplexer_3_out), .sel(xnor_1_out));
  Adder #(.width(5)) adder_1 (.a(\µPC_q ), .b(5'b00001), .out(adder_1_out));  // open: cin, cout
  Counter #(.width(10), .max('h3ff)) u_CICN (.count(1'b1), .Q(CICN), .clk(clk), .clr(reset));  // open: load, D, carry
  Register #(.width(5)) \u_µPC  (.D(multiplexer_3_out), .Q(\µPC_q ), .clk(clk), .clr(reset));  // open: en
  Adder #(.width(7)) adder_2 (.a(7'b0000001), .b(A), .out(adder_2_out));  // open: cin, cout
  Register #(.width(16)) u_A (.D(ram_1_data), .en(a_t), .Q(A_q), .clk(clk));  // open: clr
  Register #(.width(1)) u_FZ (.D(alu_1_z), .en(fz_t), .Q(FZ), .clk(clk));  // open: clr
  ROM #(.addrWidth(5), .dataWidth(19)) rom_1 (
    .addr(\µPC_q ),
    .data({rom_1_data_3, rom_1_data_2[13], rom_1_data, mux, alu, nL_E, pc_t, ir, a_t, b, fz_t}));  // open: sel
  Comparator #(.width(5)) comparator_1 (.a(5'b00001), .b(\µPC_q ), .eq(comparator_1_eq));  // open: gt, lt
  ALU alu_1 (.A(A_q), .B(B_q), .T(alu), .out({alu_1_out, D6_0}), .Z(alu_1_z));  // open: N, C, V
  Register #(.width(16)) u_B (.D(ram_1_data), .en(b), .Q(B_q), .clk(clk));  // open: clr
  RAM #(.addrWidth(7), .dataWidth(16), .bus("separate")) ram_1 (
    .addr(A), .din({alu_1_out, D6_0}), .data(ram_1_data), .str(nL_E), .sel(1'b1), .clk(clk), .ld(not_1_out));  // open: clr
  not not_1 (not_1_out, nL_E);
  // Probe on PC
  Button button_1 (.out(reset));
  Clock clock_1 (.out(clk));
  // Probe on {CO[1:0], F}
  // Probe on CO
  // Probe on D
  Counter #(.width(10), .max('h3ff)) u_INSN (
    .count(comparator_1_eq), .Q(INSN), .clk(clk), .clr(reset));  // open: load, D, carry
  // Probe on CICN
  // Probe on INSN
  TTY tty_1 (.data(D6_0), .clk(clk), .we(tty_out_1_out), .clr(tty_out_1_clr));
  tty_out tty_out_1 (.A(A), .E(nL_E), .out(tty_out_1_out), .clr(tty_out_1_clr), .D(D6_0), .clk(clk));

  // Other names for the same wires on the sheet: F[6:5] = CO[1:0]

  // Notes on the sheet:
  //   Unidad de control microprogramada (14 micro instrucciones)
  //   Unidad de Proceso (ruta de datos)
  //   contents of rom_1 (hex, n*v repeats v):
  //   3c18 22800 1ac00 3e02 3f04 1f21 3e02 1fa1 32c00 3e02 3f04 1c41 42000 3e400 1000 5f18 41c00
  //   Control de simulación
  //   0 ADD
  //   1 CMP
  //   2 MOV
  //   3 BEQ
endmodule

module tty_out (
  input  clk,
  input  [6:0] A,
  input  E,
  input  [6:0] D,
  output out,
  output clr
);

  wire and_2_out, and_3_out;

  and and_1 (out, A[0], A[1], A[2], A[3], A[4], A[5], A[6], E);
  and and_2 (and_2_out, ~D[0], ~D[1], ~D[2], ~D[3], ~D[4], ~D[5], ~D[6]);  // AND_Gate
  and and_3 (and_3_out, out, and_2_out);
  D_Flip_Flop d_ff_1 (.clk(clk), .D(and_3_out), .Q(clr), .en(1'b1));  // open: Qn, preset, reset
endmodule

module ALU (
  input  [1:0] T,
  input  [15:0] A,
  input  [15:0] B,
  output [15:0] out,
  output N,
  output C,
  output Z,
  output V
);

  wire and_1_out, and_2_out, not_1_out, not_2_out, not_3_out;
  wire [15:0] adder_1_out, xor_1_out, xor_2_out;

  not not_1 (not_1_out, A[15]);
  assign xor_1_out = A ^ B;  // XOR_Gate xor_1, 16 bits wide
  assign xor_2_out = B ^ {16{T[1]}};  // XOR_Gate xor_2, 16 bits wide
  Adder #(.width(16)) adder_1 (.a(A), .b(xor_2_out), .out(adder_1_out), .cin(T[1]), .cout(C));
  not not_2 (not_2_out, xor_2_out[15]);
  not not_3 (not_3_out, N);
  and and_1 (and_1_out, A[15], xor_2_out[15], not_3_out);
  and and_2 (and_2_out, not_1_out, not_2_out, N);
  mux2 mux2_1 (.S0(T[0]), .S1(T[1]), .X0(adder_1_out), .X1(xor_1_out), .X2(B), .X3(adder_1_out), .Z({N, out[14:0]}));
  or or_1 (V, and_1_out, and_2_out);
  nor nor_1 (Z, out[0], out[1], out[2], out[3], out[4], out[5], out[6], out[7], out[9], out[10], out[11], out[12], out[13], out[14], N, out[8]);

  assign out[15] = N;
endmodule

module mux1 (
  input  S0,
  input  S1,
  input  X0,
  input  X1,
  input  X2,
  input  X3,
  output z
);

  wire and_1_out, and_2_out, and_3_out, and_4_out, not_1_out, not_2_out;

  not not_1 (not_1_out, S0);
  not not_2 (not_2_out, S1);
  and and_1 (and_1_out, X0, not_2_out, not_1_out);
  and and_2 (and_2_out, X1, not_2_out, S0);
  and and_3 (and_3_out, X2, S1, not_1_out);
  and and_4 (and_4_out, X3, S0, S1);
  or or_1 (z, and_1_out, and_2_out, and_3_out, and_4_out);
endmodule

module mux2 (
  input  S0,
  input  S1,
  input  [15:0] X0,
  input  [15:0] X1,
  input  [15:0] X2,
  input  [15:0] X3,
  output [15:0] Z
);

  mux1 mux1_1 (.S0(S0), .S1(S1), .X0(X0[0]), .X1(X1[0]), .X2(X2[0]), .X3(X3[0]), .z(Z[0]));
  mux1 mux1_2 (.S0(S0), .S1(S1), .X0(X0[1]), .X1(X1[1]), .X2(X2[1]), .X3(X3[1]), .z(Z[1]));
  mux1 mux1_3 (.S0(S0), .S1(S1), .X0(X0[2]), .X1(X1[2]), .X2(X2[2]), .X3(X3[2]), .z(Z[2]));
  mux1 mux1_4 (.S0(S0), .S1(S1), .X0(X0[3]), .X1(X1[3]), .X2(X2[3]), .X3(X3[3]), .z(Z[3]));
  mux1 mux1_5 (.S0(S0), .S1(S1), .X0(X0[4]), .X1(X1[4]), .X2(X2[4]), .X3(X3[4]), .z(Z[4]));
  mux1 mux1_6 (.S0(S0), .S1(S1), .X0(X0[5]), .X1(X1[5]), .X2(X2[5]), .X3(X3[5]), .z(Z[5]));
  mux1 mux1_7 (.S0(S0), .S1(S1), .X0(X0[6]), .X1(X1[6]), .X2(X2[6]), .X3(X3[6]), .z(Z[6]));
  mux1 mux1_8 (.S0(S0), .S1(S1), .X0(X0[7]), .X1(X1[7]), .X2(X2[7]), .X3(X3[7]), .z(Z[7]));
  mux1 mux1_9 (.S0(S0), .S1(S1), .X0(X0[8]), .X1(X1[8]), .X2(X2[8]), .X3(X3[8]), .z(Z[8]));
  mux1 mux1_10 (.S0(S0), .S1(S1), .X0(X0[9]), .X1(X1[9]), .X2(X2[9]), .X3(X3[9]), .z(Z[9]));
  mux1 mux1_11 (.S0(S0), .S1(S1), .X0(X0[10]), .X1(X1[10]), .X2(X2[10]), .X3(X3[10]), .z(Z[10]));
  mux1 mux1_12 (.S0(S0), .S1(S1), .X0(X0[11]), .X1(X1[11]), .X2(X2[11]), .X3(X3[11]), .z(Z[11]));
  mux1 mux1_13 (.S0(S0), .S1(S1), .X0(X0[12]), .X1(X1[12]), .X2(X2[12]), .X3(X3[12]), .z(Z[12]));
  mux1 mux1_14 (.S0(S0), .S1(S1), .X0(X0[13]), .X1(X1[13]), .X2(X2[13]), .X3(X3[13]), .z(Z[13]));
  mux1 mux1_15 (.S0(S0), .S1(S1), .X0(X0[14]), .X1(X1[14]), .X2(X2[14]), .X3(X3[14]), .z(Z[14]));
  mux1 mux1_16 (.S0(S0), .S1(S1), .X0(X0[15]), .X1(X1[15]), .X2(X2[15]), .X3(X3[15]), .z(Z[15]));
endmodule
